# Fritzing sketch lcd_wiring (saved by Fritzing 0.9.3b)

parts:
  Raspberry_Pi1 = Raspberry Pi B+
  LCD1 = LCD screen

nets:
  N1: Raspberry_Pi1.3v3, LCD1.LED+
  N2: Raspberry_Pi1.GPIO27, LCD1.A0
  N3: Raspberry_Pi1.GPIO22, LCD1.RESET
  N4: Raspberry_Pi1.GPIO10, LCD1.SDA
  N5: Raspberry_Pi1.GPIO11, LCD1.SCL
  GND: Raspberry_Pi1.GND, LCD1.GND, LCD1.LED-
  N6: Raspberry_Pi1.GPIO8, LCD1.CS
  5V: Raspberry_Pi1.5V, LCD1.VCC

custom parts:
  LCD screen: A standard character display, usually with 2x16 characters. Comes in many colors.
